# Fritzing sketch beed-room-clock Sketch (saved by Fritzing 0.9.4)
breadboards: 1

parts:
  M1 = DOIT Esp32 DevKit v1 (30 pins long, 11 pins width) [part_number=ESP32S-PIN30]
  hc-sr1 = hc-sr04
  OLED1 = OLED 128x64 I2C Monochrome Display
  DHT1 = DHT22 Humidity and Temperature Sensor
  R1 = Resistor [tolerance=±5% resistance=4.7k package="0402 [SMD]"]

nets:
  3V3: M1.3V3, DHT1.VDD, R1.Pin_1
  GND: M1.GND, hc-sr1.GND, OLED1.GND, DHT1.GND
  N1: M1.D4, DHT1.DATA, R1.Pin_0
  N2: M1.D5, hc-sr1.Trig
  N3: M1.D18, hc-sr1.Echo
  N4: M1.D21, OLED1.SDA
  N5: M1.D22, OLED1.SCK
  VIN: M1.VIN, hc-sr1.VCC, OLED1.VDD

custom parts:
  DOIT Esp32 DevKit v1 (30 pins long, 11 pins width): The DOIT Esp32 DevKit v1 is one of the development board created by DOIT to evaluate the ESP-WROOM-32 module. It is based on the ESP32 microcontroller that boasts Wifi, Bluetooth, Ethernet and Low Power support all in a single chip. (vanepp) made breadboard work, adjusted pin numbering and labels and reduced size of schematic and cleaned up pcb. This chip is 30pins long (2 x15) and 11 pins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
